# Fritzing sketch SmileyPanel (saved by Fritzing 0.9.4)
breadboards: 2

parts:
  M1 = DOIT Esp32 DevKit v1 (30 pins long, 11 pins width) [part_number=ESP32S-PIN30]
  LED1 = LED - 5mm [color="Red (633nm)" package="5 mm [THT]"]
  LED2 = LED - 5mm [color="Red (633nm)" package="5 mm [THT]"]
  S1 = Pushbutton [package="[THT]"]
  S2 = Pushbutton [package="[THT]"]
  S3 = Pushbutton [package="[THT]"]
  S4 = Pushbutton [package="[THT]"]
  LED3 = LED - 5mm [color="Red (633nm)" package="5 mm [THT]"]
  LED4 = LED - 5mm [color="Red (633nm)" package="5 mm [THT]"]
  R1 = Resistor [tolerance=±5% resistance=4.70 package=THT]
  R2 = Resistor [tolerance=±5% resistance=4.70 package=THT]
  R3 = Resistor [tolerance=±5% resistance=4.70 package=THT]
  R4 = Resistor [tolerance=±5% resistance=4.70 package=THT]
  R5 = Resistor [tolerance=±5% resistance=220 package=THT]
  R6 = Resistor [tolerance=±5% resistance=220 package=THT]
  R7 = Resistor [tolerance=±5% resistance=220 package=THT]
  R8 = Resistor [tolerance=±5% resistance=220 package=THT]

nets:
  N1: M1.3V3, S1.Pin_1, S1.Pin_2, S2.Pin_1, S2.Pin_2, S3.Pin_1, S3.Pin_2, S4.Pin_1, S4.Pin_2
  N2: M1.GND, LED1.cathode, LED2.cathode, LED3.cathode, LED4.cathode, R1.Pin_0, R2.Pin_0, R3.Pin_0, R4.Pin_0
  N3: M1.D19, R5.Pin_1
  N4: M1.D21, R8.Pin_1
  N5: M1.D22, R7.Pin_1
  N6: M1.D23, R6.Pin_1
  N7: M1.VP, S2.Pin_3, S2.Pin_4, R1.Pin_1
  N8: M1.VN, S3.Pin_3, S3.Pin_4, R2.Pin_1
  N9: M1.D34, S4.Pin_3, S4.Pin_4, R3.Pin_1
  N10: M1.D35, S1.Pin_3, S1.Pin_4, R4.Pin_1
  N11: LED1.anode, R6.Pin_0
  N12: LED2.anode, R7.Pin_0
  N13: LED3.anode, R8.Pin_0
  N14: LED4.anode, R5.Pin_0

custom parts:
  DOIT Esp32 DevKit v1 (30 pins long, 11 pins width): The DOIT Esp32 DevKit v1 is one of the development board created by DOIT to evaluate the ESP-WROOM-32 module. It is based on the ESP32 microcontroller that boasts Wifi, Bluetooth, Ethernet and Low Power support all in a single chip. (vanepp) made breadboard work, adjusted pin numbering and labels and reduced size of schematic and cleaned up pcb. This chip is 30pins long (2 x15) and 11 pins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
